# Fritzing sketch WicdCO2 (saved by Fritzing 1.0.6)
circuit board: 17.7344cm x 6.5702cm

parts:
  Part1 = Adafruit SCD30 [part_number="Adafruit #4867"]
  Adafruit_Proto_Doubler_PiCowbell1 = Adafruit Proto Doubler PiCowbell [part_number=#5906]
  A2 = Raspberry Pi Pico2
  Adafruit_PiCowbell_Adalogger2 = Adafruit PiCowbell Adalogger [part_number=#5703]

nets:
  GND: Part1.GND, Adafruit_Proto_Doubler_PiCowbell1.GND, A2.pin_23, A2.pin_28, A2.pin_33, Adafruit_PiCowbell_Adalogger2.GND
  3.3V: Part1.VCC, Adafruit_Proto_Doubler_PiCowbell1.3.3V, A2.pin_37, Adafruit_PiCowbell_Adalogger2.3.3V
  N1: Part1.SDA, Adafruit_Proto_Doubler_PiCowbell1.IO5, A2.pin_7, Adafruit_PiCowbell_Adalogger2.SDA
  N2: Part1.SCL, Adafruit_Proto_Doubler_PiCowbell1.IO4, A2.pin_6, Adafruit_PiCowbell_Adalogger2.SCL
  N3: Part1.RDY, Adafruit_Proto_Doubler_PiCowbell1.IO6, A2.pin_9

custom parts:
  Adafruit Proto Doubler PiCowbell: The Adafruit Proto Doubler PiCowBell is intended to be treated like a mini solder-less proto plate to simplify programming and sensor connectivity for your Raspberry Pi Pico board. Reset button? Yes! STEMMA QT / Qwiic connector for fast I2C? Indeed. Battery with recharging and on/off switch? Affirmative. Plug-and-play so no soldering necessary when used with a Pico H or Pico WH? Here you go!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
  Raspberry Pi Pico2: Raspberry Pi Pico 2W is our new $7 microcontroller board, built on RP2350: our new high-performance, secure microcontroller with on board WiFi.
  Adafruit PiCowbell Adalogger: Ding dong! Hear that? It's the PiCowbell ringing, letting you know that the new Adafruit PiCowbell Adalogger is in stock and ready to assist your Raspberry Pi Pico and Pico W project with handy hardware and datalogging. The PiCowbell Adalogger is the same size and shape as a Pico and is intended to socket underneath to make your next data logging or data reading project super easy. Micro SD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
